# Fritzing sketch Picture (saved by Fritzing 0.9.3b)

parts:
  LCM1602_IIC1 = LCM1602 IIC [part_number="LCM1602 IIC" chip_label="LCM1602 IIC" package="DIP (Dual Inline) [THT]"]
  Part1 = Arduino Uno (Rev3)
  J1 = Piezo Speaker
  LCD1 = LCD screen
  PIR1 = PIR sensor
  S1 = Pushbutton [package="[THT]"]
  LED1 = smd LED [color="Red (633nm)" package="0603 [SMD]"]
  LED2 = smd LED [color="Orange (612nm)" package="0603 [SMD]"]
  LED3 = smd LED [color="Green (565nm)" package="0603 [SMD]"]
  JACK1 = 2.1mm Barrel Jack with Terminal Block
  Part2 = RFID-RC522 [part_number=101218]
  SERVO1 = Tower Pro SG90 servo [part_number=101246]
  R1 = Resistor [tolerance=±5% resistance=220 package="0402 [SMD]"]  # not connected
  R2 = Resistor [tolerance=±5% resistance=220 package="0402 [SMD]"]  # not connected
  R3 = Resistor [tolerance=±5% resistance=220 package="0402 [SMD]"]  # not connected

nets:
  VSS: LCM1602_IIC1.VSS, LCD1.VSS
  VDD: LCM1602_IIC1.VDD, LCD1.VDD
  N1: LCM1602_IIC1.V0, LCD1.V0
  N2: LCM1602_IIC1.RS, LCD1.RS
  N3: LCM1602_IIC1.RW, LCD1.R/W
  N4: LCM1602_IIC1.E, LCD1.E
  N5: LCM1602_IIC1.D0, LCD1.DB0
  N6: LCM1602_IIC1.D1, LCD1.DB1
  N7: LCM1602_IIC1.D2, LCD1.DB2
  N8: LCM1602_IIC1.D3, LCD1.DB3
  N9: LCM1602_IIC1.D4, LCD1.DB4
  N10: LCM1602_IIC1.D5, LCD1.DB5
  N11: LCM1602_IIC1.D6, LCD1.DB6
  N12: LCM1602_IIC1.D7, LCD1.DB7
  N13: LCM1602_IIC1.A, LCD1.LED+
  N14: LCM1602_IIC1.K, LCD1.LED-
  GND: LCM1602_IIC1.GND, Part1.GND, JACK1.NEG, Part2.GND
  VCC: LCM1602_IIC1.VCC, Part1.5V
  N15: LCM1602_IIC1.SDA, Part1.A4/SDA
  N16: LCM1602_IIC1.SCL, Part1.A5/SCL
  N17: Part1.D8, SERVO1.Signal
  N18: Part1.D9_PWM, Part2.RST
  N19: Part1.D10_PWM/SS, Part2.SDA
  N20: Part1.D11_PWM/MOSI, Part2.MOSI
  N21: Part1.D12/MISO, Part2.MISO
  N22: Part1.D13/SCK, Part2.SCK
  N23: Part1.D2, PIR1.SIG
  N24: Part1.D3_PWM, S1.Pin_4
  N25: Part1.D4, J1.pin2
  N26: Part1.D5_PWM, LED3.cathode
  N27: Part1.D6_PWM, LED2.cathode
  N28: Part1.D7, LED1.cathode
  3V3: Part1.3V3, Part2.3.3V
  N29: Part1.VIN, JACK1.POS
  N30: J1.pin1, S1.Pin_2

custom parts:
  LCM1602 IIC: I2C-Module to use a 1602 or 2004 LCD on with the wire.h libory Serial LCD Modul
  Tower Pro SG90 servo: Original file by John De Cristofaro http://www.adafruit.com/products/1449 Adafruit Feedback Servo (Small) Edited by: e-radionica.com 28/9/2015
