# Fritzing sketch Picture (saved by Fritzing 0.9.3b)

parts:
  LCM1602_IIC1 = LCM1602 IIC [part_number="LCM1602 IIC" chip_label="LCM1602 IIC" package="DIP (Dual Inline) [THT]"]
  LCD1 = LCD screen
  Part1 = Arduino Nano (Rev3.0)
  HC-SR04_Sensor_1 = HC-SR04 Ultrasonic Distance Sensor
  DFRobot_DFPlayer_Mini1 = DFRobot DFPlayer Mini [part_number=DFR0299]
  AMP1 = PAM8403 6W Stereo Amplifier
  U1 = MLX90614 [package=to-39]  # not connected
  SPKR1 = Loudspeaker  # not connected
  U2 = SWITCH-SPST-2 [package=switch-spst-vertical]
  JACK1 = 2.1mm Barrel Jack with Terminal Block
  R1 = Resistor [tolerance=±5% resistance=1k package=THT]  # not connected
  LED1 = smd LED [color="Red (633nm)" package="1206 [SMD]"]
  LED2 = smd LED [color="Orange (620nm)" package="1206 [SMD]"]
  LED3 = smd LED [color="Green (570nm)" package="1206 [SMD]"]

nets:
  VSS: LCM1602_IIC1.VSS, LCD1.VSS
  VDD: LCM1602_IIC1.VDD, LCD1.VDD
  N1: LCM1602_IIC1.V0, LCD1.V0
  N2: LCM1602_IIC1.RS, LCD1.RS
  N3: LCM1602_IIC1.RW, LCD1.R/W
  N4: LCM1602_IIC1.E, LCD1.E
  N5: LCM1602_IIC1.D0, LCD1.DB0
  N6: LCM1602_IIC1.D1, LCD1.DB1
  N7: LCM1602_IIC1.D2, LCD1.DB2
  N8: LCM1602_IIC1.D3, LCD1.DB3
  N9: LCM1602_IIC1.D4, LCD1.DB4
  N10: LCM1602_IIC1.D5, LCD1.DB5
  N11: LCM1602_IIC1.D6, LCD1.DB6
  N12: LCM1602_IIC1.D7, LCD1.DB7
  N13: LCM1602_IIC1.A, LCD1.LED+
  N14: LCM1602_IIC1.K, LCD1.LED-
  VCC: LCM1602_IIC1.VCC, Part1.5V, HC-SR04_Sensor_1.VCC
  N15: LCM1602_IIC1.SDA, Part1.A4
  N16: LCM1602_IIC1.SCL, Part1.A5
  N17: LCM1602_IIC1.LED_A, LCM1602_IIC1.LED_B
  N18: Part1.D4, LED1.anode
  N19: Part1.D5, LED2.anode
  N20: Part1.D6, LED3.anode
  N21: Part1.D9, HC-SR04_Sensor_1.TRIG
  N22: Part1.D10, HC-SR04_Sensor_1.ECHO
  N23: Part1.D12/MISO, DFRobot_DFPlayer_Mini1.TX
  N24: Part1.VIN, U2.P
  N25: Part1.GND, JACK1.NEG
  N26: DFRobot_DFPlayer_Mini1.DAC_R, AMP1.INPUTL
  N27: DFRobot_DFPlayer_Mini1.DAC_L, AMP1.INPUTG
  N28: U2.O, JACK1.POS

custom parts:
  LCM1602 IIC: I2C-Module to use a 1602 or 2004 LCD on with the wire.h libory Serial LCD Modul
  HC-SR04 Ultrasonic Distance Sensor: The HC-SR04 is an ultrasonic distance sensor. It is capable of providing measurement for ranges of 2cm to 400cm. The module operates at 5V.
  PAM8403 6W Stereo Amplifier: PAM8403 6 Watt Stereo Amplifier
