# Fritzing sketch Blynk (saved by Fritzing 0.9.3b)

parts:
  1_Channel_Relay1 = 1 Channel Power Relay
  1_Channel_Relay2 = 1 Channel Power Relay
  U2 = NodeMCU V3.0
  LED1 = LEDs [package=led10mm]
  LED2 = LEDs [package=led10mm]

nets:
  N1: 1_Channel_Relay1.IN, U2.D0
  N2: 1_Channel_Relay1.NC, LED1.A
  N3: 1_Channel_Relay1.COM, 1_Channel_Relay2.COM
  N4: 1_Channel_Relay2.VCC, U2.VU
  GND: 1_Channel_Relay2.GND, U2.GND
  N5: 1_Channel_Relay2.IN, U2.D1
  N6: 1_Channel_Relay2.NC, LED2.A
  N7: LED1.C, LED2.C

notes:
  AC
  220V

custom parts:
  1 Channel Power Relay: A 1 channel power relay. The module operates at 5V.
  NodeMCU V3.0: ESP8266 based NodeMCU
  LEDs: LEDs Standard schematic elements and footprints for 5mm, 3mm, 1206, and 0603 sized LEDs. 5mm - Spark Fun Electronics SKU : COM-00529 (and others)
