# Fritzing sketch Picture (saved by Fritzing 0.9.3b)

parts:
  U1 = NodeMCU V1.0
  LCM1602_IIC1 = LCM1602 IIC [part_number="LCM1602 IIC" chip_label="LCM1602 IIC" package="DIP (Dual Inline) [THT]"]
  LCD1 = 16x4 LCD display [part_number=1604A]

nets:
  GND: U1.D1, U1.GND, U1.TX, LCM1602_IIC1.GND, LCM1602_IIC1.SCL
  N1: U1.D2, LCM1602_IIC1.SDA
  N2: U1.RSV, LCM1602_IIC1.VCC
  VSS: LCM1602_IIC1.VSS, LCD1.Vss
  VDD: LCM1602_IIC1.VDD, LCD1.Vdd
  N3: LCM1602_IIC1.V0, LCD1.Vo
  N4: LCM1602_IIC1.RS, LCD1.RS
  N5: LCM1602_IIC1.RW, LCD1.R/W
  N6: LCM1602_IIC1.E, LCD1.E
  N7: LCM1602_IIC1.D0, LCD1.DB0
  N8: LCM1602_IIC1.D1, LCD1.DB1
  N9: LCM1602_IIC1.D2, LCD1.DB2
  N10: LCM1602_IIC1.D3, LCD1.DB3
  N11: LCM1602_IIC1.D4, LCD1.DB4
  N12: LCM1602_IIC1.D5, LCD1.DB5
  N13: LCM1602_IIC1.D6, LCD1.DB6
  N14: LCM1602_IIC1.D7, LCD1.DB7
  N15: LCM1602_IIC1.A, LCD1.LED+
  N16: LCM1602_IIC1.K, LCD1.LED-
  N17: LCM1602_IIC1.LED_A, LCM1602_IIC1.LED_B

custom parts:
  NodeMCU V1.0: ESP8266 based NodeMCU V1.0
  LCM1602 IIC: I2C-Module to use a 1602 or 2004 LCD on with the wire.h libory Serial LCD Modul
  16x4 LCD display: 16x4 character display. CHECK LED POLARITY BEFORE CONNECTING POWER Some versions of the display have the polarity of the LED pins "A" and "K" reversed.
