# Fritzing sketch Picture (saved by Fritzing 0.9.3b)

parts:
  GLCD_128x1 = 128 x 64 Graphic LCD
  Part4 = Real Time Clock Module - DS1307 RTC Breakout Board
  Part5 = Arduino Uno (Rev3)

nets:
  N1: GLCD_128x1.4_D/I, Part5.D10_PWM/SS
  N2: GLCD_128x1.5_R/W, Part5.D11_PWM/MOSI
  GND: GLCD_128x1.15_CS1, Part4.GND, Part5.GND
  N3: GLCD_128x1.17_RST, Part5.D12/MISO
  N4: GLCD_128x1.19_A(+), Part5.3V3
  5V: Part4.5V, Part5.5V
  N5: Part4.SCL, Part5.A5/SCL
  N6: Part4.SDA, Part5.A4/SDA

notes:
  DS1307
  (ST7920)
  BUK BLA RST NC PSB DB7 DB6 DB5 DB4 DB3 DB2 DB1 DB0 E P/W RS V0 VCC GND
