# Fritzing sketch Picture (saved by Fritzing 0.9.3b)

parts:
  Part1 = LCD1602-I2C
  Part2 = Arduino Uno (Rev3) - ICSP
  Part3 = MQ-3 breakout
  T1 = LM35 Temperature Sensor [package="TO92 [THT]"]
  KY-1 = Keyes Relay [package=THT]
  J1 = Piezo Speaker

nets:
  GND: Part1.GND, Part2.GND, KY-1.power, KY-1.ground
  VCC: Part1.VCC, Part2.5V
  N1: Part1.SDA, Part2.A4/SDA
  N2: Part1.SCL, Part2.A5/SCL
  N3: Part2.A0, T1.Vout
  N4: Part2.A1, Part3.AO
  N5: Part2.D8, Part3.DO
  N6: Part2.D9_PWM, KY-1.signal
  N7: KY-1.NO, J1.pin2

notes:
  MQ2

custom parts:
  LCD1602-I2C: A standard character display, usually with 2x16 characters. Comes in many colors with LCM1602 IIC attached.
  MQ-3 breakout: Alcohol sensor is capable of detecting alcohol (ethanol) particles on itself and gives the information in digital form back to us to manipulate with it. SKU:101251 • Voltage: 5V DC • Power: max 750mW • Measurement range: 0.04-4mg/L
  Keyes Relay: The Keyes 5V relay module is suitable for SCM development, home appliance control. It uses a 5V~12V TIL control signal which can control DC / AC signal.
